// Logisim project circuit1.circ as structural Verilog: 5 circuits, main circuit main
module main (
  input  sw3,
  input  sw2,
  input  sw1,
  input  sw0,
  input  sw7,
  input  sw6,
  input  sw5,
  input  sw4,
  input  sw11,
  input  sw10,
  input  sw9,
  input  sw8,
  input  sw15,
  input  sw14,
  input  sw13,
  input  sw12,
  input  btnR,
  input  btnD,
  input  btnL,
  input  btnU
);

  wire \n2_4线程管理_1_y0 , \n2_4线程管理_1_y1 , \n2_4线程管理_1_y2 , \n2_4线程管理_1_y3 , \n4输入优先编码器_1_w0 ,
       \n4输入优先编码器_1_w1 , n7_led_1_a0, n7_led_1_b0, n7_led_1_c0, n7_led_1_d0, n7_led_1_e0, n7_led_1_f0,
       n7_led_1_g0, n7_led_2_a0, n7_led_2_b0, n7_led_2_c0, n7_led_2_d0, n7_led_2_e0, n7_led_2_f0,
       n7_led_2_g0, n7_led_3_a0, n7_led_3_b0, n7_led_3_c0, n7_led_3_d0, n7_led_3_e0, n7_led_3_f0,
       n7_led_3_g0, n7_led_4_a0, n7_led_4_b0, n7_led_4_c0, n7_led_4_d0, n7_led_4_e0, n7_led_4_f0,
       n7_led_4_g0, not_1_out, not_2_out, not_3_out, not_4_out, not_5_out, not_6_out, not_7_out, not_8_out,
       not_9_out, not_10_out, not_11_out, not_12_out, not_13_out, not_14_out, not_15_out, not_16_out,
       not_17_out, not_18_out, not_19_out, not_20_out, not_21_out, not_22_out, not_23_out, not_24_out,
       not_25_out, not_26_out, not_27_out, not_28_out, or_1_out, showchar_1_a, showchar_1_b, showchar_1_c,
       showchar_1_d, showchar_1_e, showchar_1_f, showchar_1_g, showchar_2_a, showchar_2_b, showchar_2_c,
       showchar_2_d, showchar_2_e, showchar_2_f, showchar_2_g, showchar_3_a, showchar_3_b, showchar_3_c,
       showchar_3_d, showchar_3_e, showchar_3_f, showchar_3_g, showchar_4_a, showchar_4_b, showchar_4_c,
       showchar_4_d, showchar_4_e, showchar_4_f, showchar_4_g;

  or or_1 (or_1_out, btnR, btnD, btnL, btnU);
  \_4输入优先编码器  \u_4输入优先编码器_1  (.b3(btnR), .b2(btnD), .b1(btnL), .b0(btnU), .W1(\n4输入优先编码器_1_w1 ), .W0(\n4输入优先编码器_1_w0 ));
  \_2_4线程管理  \u_2_4线程管理_1  (
    .Enable(or_1_out), .w1(\n4输入优先编码器_1_w1 ), .w0(\n4输入优先编码器_1_w0 ), .Y0(\n2_4线程管理_1_y0 ),
    .Y1(\n2_4线程管理_1_y1 ), .Y2(\n2_4线程管理_1_y2 ), .Y3(\n2_4线程管理_1_y3 ));
  SHOWCHAR showchar_1 (
    .sw3(sw3), .sw2(sw2), .sw1(sw1), .sw0(sw0), .a(showchar_1_a), .b(showchar_1_b), .c(showchar_1_c),
    .d(showchar_1_d), .e(showchar_1_e), .f(showchar_1_f), .g(showchar_1_g));
  SHOWCHAR showchar_2 (
    .sw3(sw7), .sw2(sw6), .sw1(sw5), .sw0(sw4), .a(showchar_2_a), .b(showchar_2_b), .c(showchar_2_c),
    .d(showchar_2_d), .e(showchar_2_e), .f(showchar_2_f), .g(showchar_2_g));
  SHOWCHAR showchar_3 (
    .sw3(sw11), .sw2(sw10), .sw1(sw9), .sw0(sw8), .a(showchar_3_a), .b(showchar_3_b), .c(showchar_3_c),
    .d(showchar_3_d), .e(showchar_3_e), .f(showchar_3_f), .g(showchar_3_g));
  SHOWCHAR showchar_4 (
    .sw3(sw15), .sw2(sw14), .sw1(sw13), .sw0(sw12), .a(showchar_4_a), .b(showchar_4_b), .c(showchar_4_c),
    .d(showchar_4_d), .e(showchar_4_e), .f(showchar_4_f), .g(showchar_4_g));
  not not_1 (not_1_out, showchar_1_a);
  not not_2 (not_2_out, showchar_1_b);
  not not_3 (not_3_out, showchar_1_c);
  not not_4 (not_4_out, showchar_1_d);
  not not_5 (not_5_out, showchar_1_e);
  not not_6 (not_6_out, showchar_1_f);
  not not_7 (not_7_out, showchar_1_g);
  not not_8 (not_8_out, showchar_2_a);
  not not_9 (not_9_out, showchar_2_b);
  not not_10 (not_10_out, showchar_2_c);
  not not_11 (not_11_out, showchar_2_d);
  not not_12 (not_12_out, showchar_2_e);
  not not_13 (not_13_out, showchar_2_f);
  not not_14 (not_14_out, showchar_2_g);
  not not_15 (not_15_out, showchar_3_a);
  not not_16 (not_16_out, showchar_3_b);
  not not_17 (not_17_out, showchar_3_c);
  not not_18 (not_18_out, showchar_3_d);
  not not_19 (not_19_out, showchar_3_e);
  not not_20 (not_20_out, showchar_3_f);
  not not_21 (not_21_out, showchar_3_g);
  not not_22 (not_22_out, showchar_4_a);
  not not_23 (not_23_out, showchar_4_b);
  not not_24 (not_24_out, showchar_4_c);
  not not_25 (not_25_out, showchar_4_d);
  not not_26 (not_26_out, showchar_4_e);
  not not_27 (not_27_out, showchar_4_f);
  not not_28 (not_28_out, showchar_4_g);
  _7_led u_7_led_1 (
    .a(not_1_out), .b(not_2_out), .c(not_3_out), .d(not_4_out), .e(not_5_out), .f(not_6_out), .g(not_7_out),
    .Enable(\n2_4线程管理_1_y0 ), .a0(n7_led_1_a0), .b0(n7_led_1_b0), .c0(n7_led_1_c0), .d0(n7_led_1_d0),
    .e0(n7_led_1_e0), .f0(n7_led_1_f0), .g0(n7_led_1_g0));
  _7_led u_7_led_2 (
    .a(not_8_out), .b(not_9_out), .c(not_10_out), .d(not_11_out), .e(not_12_out), .f(not_13_out),
    .g(not_14_out), .Enable(\n2_4线程管理_1_y1 ), .a0(n7_led_2_a0), .b0(n7_led_2_b0), .c0(n7_led_2_c0),
    .d0(n7_led_2_d0), .e0(n7_led_2_e0), .f0(n7_led_2_f0), .g0(n7_led_2_g0));
  _7_led u_7_led_3 (
    .a(not_15_out), .b(not_16_out), .c(not_17_out), .d(not_18_out), .e(not_19_out), .f(not_20_out),
    .g(not_21_out), .Enable(\n2_4线程管理_1_y2 ), .a0(n7_led_3_a0), .b0(n7_led_3_b0), .c0(n7_led_3_c0),
    .d0(n7_led_3_d0), .e0(n7_led_3_e0), .f0(n7_led_3_f0), .g0(n7_led_3_g0));
  _7_led u_7_led_4 (
    .a(not_22_out), .b(not_23_out), .c(not_24_out), .d(not_25_out), .e(not_26_out), .f(not_27_out),
    .g(not_28_out), .Enable(\n2_4线程管理_1_y3 ), .a0(n7_led_4_a0), .b0(n7_led_4_b0), .c0(n7_led_4_c0),
    .d0(n7_led_4_d0), .e0(n7_led_4_e0), .f0(n7_led_4_f0), .g0(n7_led_4_g0));
  _7_Segment_Display u_7_segment_display_1 (
    .g(n7_led_2_g0), .f(n7_led_2_f0), .a(n7_led_2_a0), .b(n7_led_2_b0), .e(n7_led_2_e0), .d(n7_led_2_d0),
    .c(n7_led_2_c0));  // open: dp
  _7_Segment_Display u_7_segment_display_2 (
    .g(n7_led_1_g0), .f(n7_led_1_f0), .a(n7_led_1_a0), .b(n7_led_1_b0), .e(n7_led_1_e0), .d(n7_led_1_d0),
    .c(n7_led_1_c0));  // open: dp
  _7_Segment_Display u_7_segment_display_3 (
    .g(n7_led_4_g0), .f(n7_led_4_f0), .a(n7_led_4_a0), .b(n7_led_4_b0), .e(n7_led_4_e0), .d(n7_led_4_d0),
    .c(n7_led_4_c0));  // open: dp
  _7_Segment_Display u_7_segment_display_4 (
    .g(n7_led_3_g0), .f(n7_led_3_f0), .a(n7_led_3_a0), .b(n7_led_3_b0), .e(n7_led_3_e0), .d(n7_led_3_d0),
    .c(n7_led_3_c0));  // open: dp
endmodule

module SHOWCHAR (
  input  sw3,
  input  sw2,
  input  sw1,
  input  sw0,
  output a,
  output b,
  output c,
  output d,
  output e,
  output f,
  output g
);

  wire and_1_out, and_2_out, and_3_out, and_4_out, and_5_out, and_6_out, and_7_out, and_8_out, and_9_out,
       and_10_out, and_11_out, and_12_out, and_13_out, and_14_out, and_15_out, and_16_out, and_17_out,
       and_18_out, and_19_out, and_20_out, and_21_out, and_22_out, and_23_out, and_24_out, and_25_out,
       not_1_out, not_2_out, not_3_out, not_4_out, not_5_out, not_6_out, not_7_out, not_8_out, not_9_out,
       not_10_out, not_11_out, not_12_out, not_13_out, not_14_out, not_15_out, not_16_out, not_17_out,
       not_18_out, not_19_out, not_20_out, not_21_out, not_22_out, not_23_out, not_24_out, not_25_out,
       not_26_out, not_27_out, not_28_out, not_29_out, not_30_out, not_31_out, not_32_out, not_33_out,
       not_34_out, not_35_out, not_36_out, not_37_out, not_38_out, not_39_out, not_40_out, not_41_out;

  not not_1 (not_1_out, sw3);
  not not_2 (not_2_out, sw2);
  not not_3 (not_3_out, sw1);
  not not_4 (not_4_out, sw3);
  not not_5 (not_5_out, sw1);
  not not_6 (not_6_out, sw0);
  not not_7 (not_7_out, sw2);
  not not_8 (not_8_out, sw1);
  not not_9 (not_9_out, sw3);
  not not_10 (not_10_out, sw1);
  not not_11 (not_11_out, sw0);
  not not_12 (not_12_out, sw0);
  not not_13 (not_13_out, sw3);
  not not_14 (not_14_out, sw2);
  not not_15 (not_15_out, sw0);
  not not_16 (not_16_out, sw0);
  not not_17 (not_17_out, sw3);
  not not_18 (not_18_out, sw2);
  not not_19 (not_19_out, sw1);
  not not_20 (not_20_out, sw3);
  not not_21 (not_21_out, sw1);
  not not_22 (not_22_out, sw0);
  not not_23 (not_23_out, sw2);
  not not_24 (not_24_out, sw0);
  not not_25 (not_25_out, sw3);
  and and_1 (and_1_out, not_25_out, sw0);
  not not_26 (not_26_out, sw2);
  not not_27 (not_27_out, sw1);
  and and_2 (and_2_out, not_26_out, not_27_out, sw0);
  not not_28 (not_28_out, sw3);
  and and_3 (and_3_out, not_28_out, sw2, not_29_out);
  not not_29 (not_29_out, sw1);
  not not_30 (not_30_out, sw3);
  not not_31 (not_31_out, sw2);
  not not_32 (not_32_out, sw3);
  not not_33 (not_33_out, sw2);
  not not_34 (not_34_out, sw3);
  not not_35 (not_35_out, sw1);
  not not_36 (not_36_out, sw3);
  not not_37 (not_37_out, sw2);
  not not_38 (not_38_out, sw1);
  not not_39 (not_39_out, sw3);
  not not_40 (not_40_out, sw1);
  not not_41 (not_41_out, sw0);
  and and_4 (and_4_out, not_1_out, not_2_out, not_3_out, sw0);
  and and_5 (and_5_out, not_4_out, sw2, not_5_out, not_6_out);
  and and_6 (and_6_out, sw3, not_7_out, sw1, sw0);
  and and_7 (and_7_out, sw3, sw2, not_8_out, sw0);
  and and_8 (and_8_out, not_9_out, sw2, not_10_out, sw0);
  and and_9 (and_9_out, sw2, sw1, not_11_out);
  and and_10 (and_10_out, sw3, sw1, sw0);
  and and_11 (and_11_out, sw3, sw2, not_12_out);
  and and_12 (and_12_out, not_13_out, not_14_out, sw1, not_15_out);
  or or_1 (c, and_12_out, and_13_out, and_14_out);
  and and_13 (and_13_out, sw3, sw2, not_16_out);
  and and_14 (and_14_out, sw3, sw2, sw1);
  and and_15 (and_15_out, not_17_out, not_18_out, not_19_out, sw0);
  and and_16 (and_16_out, not_20_out, sw2, not_21_out, not_22_out);
  and and_17 (and_17_out, sw2, sw1, sw0);
  and and_18 (and_18_out, sw3, not_23_out, sw1, not_24_out);
  or or_2 (e, and_1_out, and_2_out, and_3_out);
  and and_19 (and_19_out, not_30_out, not_31_out, sw0);
  and and_20 (and_20_out, not_32_out, not_33_out, sw1);
  and and_21 (and_21_out, not_34_out, sw1, sw0);
  and and_22 (and_22_out, sw3, sw2, not_35_out, sw0);
  and and_23 (and_23_out, not_36_out, not_37_out, not_38_out);
  or or_3 (g, and_23_out, and_24_out, and_25_out);
  and and_24 (and_24_out, not_39_out, sw2, sw1, sw0);
  and and_25 (and_25_out, sw3, sw2, not_40_out, not_41_out);
  or or_4 (a, and_4_out, and_5_out, and_6_out, and_7_out);
  or or_5 (b, and_8_out, and_9_out, and_10_out, and_11_out);
  or or_6 (d, and_15_out, and_16_out, and_17_out, and_18_out);
  or or_7 (f, and_19_out, and_20_out, and_21_out, and_22_out);
endmodule

module _7_led (
  input  a,
  input  b,
  input  c,
  input  d,
  input  e,
  input  f,
  input  g,
  input  Enable,
  output a0,
  output b0,
  output c0,
  output d0,
  output e0,
  output f0,
  output g0
);

  and and_1 (a0, a, Enable);
  and and_2 (b0, b, Enable);
  and and_3 (c0, c, Enable);
  and and_4 (d0, d, Enable);
  and and_5 (e0, e, Enable);
  and and_6 (f0, f, Enable);
  and and_7 (g0, g, Enable);
endmodule

module \_2_4线程管理  (
  input  Enable,
  input  w1,
  input  w0,
  output Y0,
  output Y1,
  output Y2,
  output Y3
);

  wire not_1_out, not_2_out;

  not not_1 (not_1_out, w1);
  not not_2 (not_2_out, w0);
  and and_1 (Y0, not_2_out, Enable, not_1_out);
  and and_2 (Y1, not_1_out, Enable, w0);
  and and_3 (Y2, w1, Enable, not_2_out);
  and and_4 (Y3, w0, Enable, w1);
endmodule

module \_4输入优先编码器  (
  input  b3,
  input  b2,
  input  b1,
  input  b0,
  output W1,
  output W0
);

  wire and_1_out, not_1_out;

  or or_1 (W1, b2, b3);
  not not_1 (not_1_out, b2);
  and and_1 (and_1_out, not_1_out, b1);
  or or_2 (W0, and_1_out, b3);
endmodule
