// Logisim project RGLED.circ as structural Verilog
module \数码管驱动  (
  input  X3,
  input  X2,
  input  X1,
  input  X0,
  output Seg_1,
  output Seg_2,
  output Seg_3,
  output Seg_4,
  output Seg_5,
  output Seg_6,
  output Seg_7
);

  wire and_1_out, and_2_out, and_3_out, and_4_out, and_5_out, and_6_out, and_7_out, and_8_out, and_9_out,
       and_10_out, and_11_out, and_12_out, and_13_out, and_14_out, and_15_out, and_16_out, not_1_out,
       not_2_out, not_3_out, not_4_out, not_5_out, not_6_out, not_7_out, not_8_out, not_9_out, not_10_out,
       not_11_out, not_12_out, not_13_out, not_14_out, not_15_out, not_16_out, not_17_out, not_18_out,
       not_19_out, not_20_out, not_21_out;

  not not_1 (not_1_out, X2);
  and and_1 (and_1_out, not_1_out, X1);
  and and_2 (and_2_out, X2, not_2_out);
  not not_2 (not_2_out, X1);
  and and_3 (and_3_out, X2, not_3_out);
  not not_3 (not_3_out, X0);
  not not_4 (not_4_out, X1);
  and and_4 (and_4_out, not_4_out, not_5_out);
  not not_5 (not_5_out, X0);
  and and_5 (and_5_out, X2, not_6_out);
  not not_6 (not_6_out, X1);
  and and_6 (and_6_out, X2, not_7_out);
  not not_7 (not_7_out, X0);
  not not_8 (not_8_out, X2);
  and and_7 (and_7_out, not_8_out, not_9_out);
  not not_9 (not_9_out, X0);
  and and_8 (and_8_out, X2, X0);
  not not_10 (not_10_out, X2);
  not not_11 (not_11_out, X1);
  and and_9 (and_9_out, not_11_out, not_12_out);
  not not_12 (not_12_out, X0);
  and and_10 (and_10_out, X1, X0);
  not not_13 (not_13_out, X2);
  and and_11 (and_11_out, not_13_out, not_14_out);
  not not_14 (not_14_out, X0);
  and and_12 (and_12_out, X1, not_15_out);
  not not_15 (not_15_out, X0);
  not not_16 (not_16_out, X2);
  and and_13 (and_13_out, not_16_out, not_17_out);
  not not_17 (not_17_out, X0);
  not not_18 (not_18_out, X2);
  and and_14 (and_14_out, not_18_out, X1);
  and and_15 (and_15_out, X1, not_19_out);
  not not_19 (not_19_out, X0);
  and and_16 (and_16_out, X2, not_20_out, X0);
  not not_20 (not_20_out, X1);
  not not_21 (not_21_out, X1);
  or or_1 (Seg_7, not_21_out, X0, X2);
  or or_2 (Seg_1, and_1_out, and_2_out, and_3_out, X3);
  or or_3 (Seg_2, and_4_out, and_5_out, and_6_out, X3);
  or or_4 (Seg_3, and_7_out, X1, and_8_out, X3);
  or or_5 (Seg_4, not_10_out, and_9_out, and_10_out);
  or or_6 (Seg_5, and_11_out, and_12_out);
  or or_7 (Seg_6, and_13_out, and_14_out, and_15_out, and_16_out, X3);
endmodule

module \数码管驱动测试  (
);

  wire clock_1_out, \数码管驱动_1_seg_1 , \数码管驱动_1_seg_2 , \数码管驱动_1_seg_3 , \数码管驱动_1_seg_4 , \数码管驱动_1_seg_5 ,
       \数码管驱动_1_seg_6 , \数码管驱动_1_seg_7 ;
  wire [3:0] counter_1_q;

  Counter #(.width(4), .max('hf), .behavior("old")) counter_1 (
    .Q(counter_1_q), .clk(clock_1_out));  // open: load, D, count, carry, clr, preset
  Clock clock_1 (.out(clock_1_out));
  \数码管驱动  \u_数码管驱动_1  (
    .X3(counter_1_q[3]), .X2(counter_1_q[2]), .Seg_1(\数码管驱动_1_seg_1 ), .X1(counter_1_q[1]),
    .X0(counter_1_q[0]), .Seg_2(\数码管驱动_1_seg_2 ), .Seg_3(\数码管驱动_1_seg_3 ), .Seg_4(\数码管驱动_1_seg_4 ),
    .Seg_5(\数码管驱动_1_seg_5 ), .Seg_6(\数码管驱动_1_seg_6 ), .Seg_7(\数码管驱动_1_seg_7 ));
  _7_Segment_Display u_7_segment_display_1 (
    .g(\数码管驱动_1_seg_1 ), .f(\数码管驱动_1_seg_2 ), .a(\数码管驱动_1_seg_3 ), .b(\数码管驱动_1_seg_4 ), .e(\数码管驱动_1_seg_5 ),
    .d(\数码管驱动_1_seg_6 ), .c(\数码管驱动_1_seg_7 ));  // open: dp

  // Notes on the sheet:
  //   Ctrl+T驱动时钟单步运行测试
endmodule

// 4位数比较器
module \_4位无符号比较器  (
  input  X3,
  input  X2,
  input  X1,
  input  X0,
  input  Y3,
  input  Y2,
  input  Y1,
  input  Y0,
  output Great,
  output Equal,
  output Less
);

  wire and_1_out, and_2_out, and_3_out, and_4_out, not_1_out, not_2_out, not_3_out, not_4_out, xnor_1_out,
       xnor_2_out, xnor_3_out, xnor_4_out, xnor_5_out, xnor_6_out, xnor_7_out, xnor_8_out, xnor_9_out,
       xnor_10_out;

  not not_1 (not_1_out, Y3);
  xnor xnor_1 (xnor_1_out, X3, Y3);
  not not_2 (not_2_out, Y2);
  xnor xnor_2 (xnor_2_out, X3, Y3);
  xnor xnor_3 (xnor_3_out, X2, Y2);
  not not_3 (not_3_out, Y1);
  xnor xnor_4 (xnor_4_out, X3, Y3);
  xnor xnor_5 (xnor_5_out, X2, Y2);
  xnor xnor_6 (xnor_6_out, X1, Y1);
  not not_4 (not_4_out, Y0);
  xnor xnor_7 (xnor_7_out, X3, Y3);
  xnor xnor_8 (xnor_8_out, X2, Y2);
  xnor xnor_9 (xnor_9_out, X1, Y1);
  xnor xnor_10 (xnor_10_out, X0, Y0);
  and and_1 (and_1_out, X3, not_1_out);
  and and_2 (and_2_out, xnor_1_out, X2, not_2_out);
  and and_3 (and_3_out, xnor_2_out, xnor_3_out, X1, not_3_out);
  and and_4 (and_4_out, xnor_4_out, xnor_5_out, xnor_6_out, X0, not_4_out);
  and and_5 (Equal, xnor_7_out, xnor_8_out, xnor_9_out, xnor_10_out);
  or or_1 (Great, and_1_out, and_2_out, and_3_out, and_4_out);
  nor nor_1 (Less, Great, Equal);
endmodule

module \_8位无符号比较器  (
  input  [7:0] X,
  input  [7:0] Y,
  output Great,
  output Equal,
  output Less
);

  wire and_1_out, and_2_out, \n4位无符号比较器_1_equal , \n4位无符号比较器_1_great , \n4位无符号比较器_1_less ,
       \n4位无符号比较器_2_great , \n4位无符号比较器_2_less ;

  // Probe on X
  // Probe on Y
  \_4位无符号比较器  \u_4位无符号比较器_1  (
    .X3(X[7]), .X2(X[6]), .X1(X[5]), .X0(X[4]), .Y3(Y[7]), .Y2(Y[6]), .Y1(Y[5]), .Y0(Y[4]),
    .Great(\n4位无符号比较器_1_great ), .Equal(\n4位无符号比较器_1_equal ), .Less(\n4位无符号比较器_1_less ));
  \_4位无符号比较器  \u_4位无符号比较器_2  (
    .X3(X[3]), .X2(X[2]), .X1(X[1]), .X0(X[0]), .Y3(Y[3]), .Y2(Y[2]), .Y1(Y[1]), .Y0(Y[0]),
    .Great(\n4位无符号比较器_2_great ), .Less(\n4位无符号比较器_2_less ));  // open: Equal
  and and_1 (and_1_out, \n4位无符号比较器_1_equal , \n4位无符号比较器_2_great );
  and and_2 (and_2_out, \n4位无符号比较器_1_equal , \n4位无符号比较器_2_less );
  or or_1 (Great, \n4位无符号比较器_1_great , and_1_out);
  or or_2 (Less, \n4位无符号比较器_1_less , and_2_out);
  nor nor_1 (Equal, Less, Great);

  // Other names for the same wires on the sheet: X0[3:0] = X[3:0]; X1[3:0] = X[7:4]; Y0[3:0] = Y[3:0];
  //   Y1[3:0] = Y[7:4]

  // Notes on the sheet:
  //   电路功能：X,Y进行无符号比较，Great=(X>Y)?1:0;
  //   输入引脚区
  //   输出引脚区
endmodule

// MUX
module \_2路选择器_1位  (
  input  X0,
  input  Sel,
  input  X1,
  output Out
);

  Multiplexer #(.enable("false")) multiplexer_1 (.in0(X0), .in1(X1), .out(Out), .sel(Sel));

  // Notes on the sheet:
  //   输入引脚区
  //   电路功能：Out=(Sel==0)?X0:X1;
  //   请勿增删改引脚，请在下方利用上方输入输出引脚的隧道标签信号构建电路，ctrl+d复制选择组件
  //   输出引脚区
endmodule

// MUX
module \_2路选择器_8位  (
  input  [7:0] X,
  input  Sel,
  input  [7:0] Y,
  output [7:0] Out
);

  // Probe on X
  // Probe on Y
  Multiplexer #(.width(8), .enable("false")) multiplexer_1 (.in0(X), .in1(Y), .out(Out), .sel(Sel));
  // Probe on Out

  // Notes on the sheet:
  //   输入引脚区
  //   电路功能：Out=(Sel==0)?X:Y;
  //   请勿增删改引脚，请在下方利用上方输入输出引脚的隧道标签信号构建电路，ctrl+d复制选择组件
  //   输出引脚区
endmodule

module \红绿灯  (
  input  in_1,
  input  in_2,
  output R1,
  output Y1,
  output [2:0] Status,
  output G1,
  output R2,
  output Y2,
  output [7:0] Timer,
  output G2
);

  wire CLK, not_1_out, not_2_out, or_2_out, or_3_out, PASS1, PASS2, RST, T1, T2, T3, T4, Y1c, Y2c, \紧急开关_p1 ,
       \紧急开关_p3 , \紧急开关_p5 , \紧急开关_p6 , \紧急情况 ;
  wire [2:0] S1B, S2B, \红绿灯状态机_自动生成_1_n0 ;
  wire [3:0] S1T, S2T;
  wire [7:0] counter_1_q, Timer1, Timer2;

  LED led_1 (.in(R1));
  LED led_2 (.in(Y1c));
  LED led_3 (.in(G1));
  Register #(.width(3), .Select("low")) \u_状态  (
    .D(\红绿灯状态机_自动生成_1_n0 ), .Q(Status), .clk(CLK), .clr(\紧急开关_p3 ));  // open: en
  _7_Segment_Display u_7_segment_display_1 (
    .g(S1T[0]), .f(S1T[1]), .a(S1T[2]), .b(S1T[3]), .e(S1B[0]), .d(S1B[1]), .c(S1B[2]));  // open: dp
  _7_Segment_Display u_7_segment_display_2 (
    .g(S2T[0]), .f(S2T[1]), .a(S2T[2]), .b(S2T[3]), .e(S2B[0]), .d(S2B[1]), .c(S2B[2]));  // open: dp
  // DipSwitch #(.NSwitches(1)) 紧急开关: pin names not known; wires that end beside it: \紧急开关_p1 , \紧急开关_p1 , \紧急开关_p3 , in_2, \紧急开关_p5 , \紧急开关_p6 , \紧急开关_p6 
  \红绿灯状态输出函数_真值表  \u_红绿灯状态输出函数_真值表_1  (
    .S2(Status[2]), .R1(R1), .S1(Status[1]), .Y1(Y1), .S0(Status[0]), .G1(G1), .R2(R2), .Y2(Y2), .G2(G2),
    .PASS1(PASS1), .PASS2(PASS2));
  LED led_4 (.in(R2));
  LED led_5 (.in(Y2c));
  LED led_6 (.in(G2));
  or or_1 (\紧急情况 , in_1, \紧急开关_p5 );
  \_8位无符号比较器  \u_8位无符号比较器_1  (.X(Timer1), .Y(8'h4), .Equal(T1));  // open: Great, Less
  \_8位无符号比较器  \u_8位无符号比较器_2  (.X(Timer1), .Y(8'h1), .Equal(T2));  // open: Great, Less
  \_8位无符号比较器  \u_8位无符号比较器_3  (.X(Timer2), .Y(8'h4), .Equal(T3));  // open: Great, Less
  \_8位无符号比较器  \u_8位无符号比较器_4  (.X(Timer2), .Y(8'h1), .Equal(T4));  // open: Great, Less
  not not_1 (not_1_out, CLK);
  D_Flip_Flop #(.Pre_Clr_Positions("LEGACY"), .NewFFLayout("false")) d_ff_1 (
    .clk(not_1_out), .D(\紧急情况 ));  // open: Q, Qn, preset, reset
  or or_2 (or_2_out, RST, T4);
  or or_3 (or_3_out, RST, T2);
  \红绿灯状态机_自动生成  \u_红绿灯状态机_自动生成_1  (
    .S2(Status[2]), .S1(Status[1]), .S0(Status[0]), .T1(T1), .T2(T2), .N2(\红绿灯状态机_自动生成_1_n0 [2]), .T3(T3),
    .T4(T4), .EMERG(\紧急情况 ), .N1(\红绿灯状态机_自动生成_1_n0 [1]), .N0(\红绿灯状态机_自动生成_1_n0 [0]));
  \双位十进制双向计数器  \u_双位十进制双向计数器_1  (
    .CLK(CLK), .\使能 (PASS1), .\异步置位控制 (or_2_out), .\异步预置 (8'h20), .\Mode_0正计数_1倒计数 (1'b1), .Q(Timer1));  // open: 进位_借位
  \双位十进制双向计数器  \u_双位十进制双向计数器_2  (
    .CLK(CLK), .\使能 (PASS2), .\异步置位控制 (or_3_out), .\异步预置 (8'h10), .\Mode_0正计数_1倒计数 (1'b1), .Q(Timer2));  // open: 进位_借位
  and and_1 (Y1c, Y1, CLK);
  and and_2 (Y2c, Y2, CLK);
  not not_2 (not_2_out, \紧急情况 );
  Clock clock_1 (.out(CLK));
  D_Flip_Flop #(.Pre_Clr_Positions("LEGACY"), .NewFFLayout("false")) d_ff_2 (
    .clk(CLK), .D(not_2_out), .Qn(RST));  // open: Q, preset, reset
  \_2路选择器_8位  \u_2路选择器_8位_1  (.X(Timer1), .Sel(PASS2), .Y(Timer2), .Out(Timer));
  // Probe on counter_1_q
  Counter counter_1 (.Q(counter_1_q), .clk(CLK));  // open: load, D, count, carry, clr, preset, down
  \数码管驱动  \u_数码管驱动_1  (
    .X3(Timer[7]), .X2(Timer[6]), .Seg_1(S2T[0]), .X1(Timer[5]), .X0(Timer[4]), .Seg_2(S2T[1]),
    .Seg_3(S2T[2]), .Seg_4(S2T[3]), .Seg_5(S2B[0]), .Seg_6(S2B[1]), .Seg_7(S2B[2]));
  \数码管驱动  \u_数码管驱动_2  (
    .X3(Timer[3]), .X2(Timer[2]), .Seg_1(S1T[0]), .X1(Timer[1]), .X0(Timer[0]), .Seg_2(S1T[1]),
    .Seg_3(S1T[2]), .Seg_4(S1T[3]), .Seg_5(S1B[0]), .Seg_6(S1B[1]), .Seg_7(S1B[2]));

  // Other names for the same wires on the sheet: E = in_1

  // Notes on the sheet:
  //   主道红绿灯
  //   测试时要求主道20秒，辅道10秒
  //   状态机现态
  //   倒计时
  //   辅道红绿灯
  //   状态机现态
  //   当前倒计时
  //   引脚区，用于EduCoder测试
  //   主道计时逻辑
  //   辅道计时逻辑
  //   控制黄灯闪烁
  //   初始化信号，第一拍为1
  //   用于预置计数器初始值
  //   时钟计数
  //   当前倒计时
endmodule

// 计数器
module \BCD双向计数器_可异步置位  (
  input  CLK,
  input  \使能 ,
  input  \异步置位控制 ,
  input  [3:0] \异步预置 ,
  input  \Mode_0正计数_1倒计数 ,
  output [3:0] \输出Q ,
  output \进位_借位 
);

  wire \bcd双向计数器状态转换_自动生成_1_n0 , \bcd双向计数器状态转换_自动生成_1_n1 , \bcd双向计数器状态转换_自动生成_1_n2 ,
       \bcd双向计数器状态转换_自动生成_1_n3 , D0, D1, D2, D3, multiplexer_1_out, not_1_out, not_2_out, not_3_out,
       not_4_out;

  Multiplexer #(.enable("false")) multiplexer_1 (.in0(1'b1), .in1(CLK), .out(multiplexer_1_out), .sel(\使能 ));
  assign {D3, D2, D1, D0} = \异步置位控制  ? \异步预置  : 4'bz;  // Controlled_Buffer controlled_buffer_1
  \BCD双向计数器状态转换_自动生成  \bcd双向计数器状态转换_自动生成_1  (
    .S3(\输出Q [3]), .S2(\输出Q [2]), .S1(\输出Q [1]), .S0(\输出Q [0]), .Mode(\Mode_0正计数_1倒计数 ),
    .N3(\bcd双向计数器状态转换_自动生成_1_n3 ), .N2(\bcd双向计数器状态转换_自动生成_1_n2 ), .N1(\bcd双向计数器状态转换_自动生成_1_n1 ),
    .N0(\bcd双向计数器状态转换_自动生成_1_n0 ));
  not not_1 (not_1_out, D3);
  not not_2 (not_2_out, D2);
  not not_3 (not_3_out, D1);
  not not_4 (not_4_out, D0);
  // Probe on \输出Q 
  D_Flip_Flop #(.Pre_Clr_Positions("LEGACY"), .NewFFLayout("false")) u_D3 (
    .clk(multiplexer_1_out), .D(\bcd双向计数器状态转换_自动生成_1_n3 ), .Q(\输出Q [3]), .preset(D3), .reset(not_1_out));  // open: Qn
  D_Flip_Flop #(.Pre_Clr_Positions("LEGACY"), .NewFFLayout("false")) u_D2 (
    .clk(multiplexer_1_out), .D(\bcd双向计数器状态转换_自动生成_1_n2 ), .Q(\输出Q [2]), .preset(D2), .reset(not_2_out));  // open: Qn
  D_Flip_Flop #(.Pre_Clr_Positions("LEGACY"), .NewFFLayout("false")) u_D1 (
    .clk(multiplexer_1_out), .D(\bcd双向计数器状态转换_自动生成_1_n1 ), .Q(\输出Q [1]), .preset(D1), .reset(not_3_out));  // open: Qn
  D_Flip_Flop #(.Pre_Clr_Positions("LEGACY"), .NewFFLayout("false")) u_D0 (
    .clk(multiplexer_1_out), .D(\bcd双向计数器状态转换_自动生成_1_n0 ), .Q(\输出Q [0]), .preset(D0), .reset(not_4_out));  // open: Qn
  \BCD双向计数器输出函数_自动生成  \bcd双向计数器输出函数_自动生成_1  (
    .S3(\输出Q [3]), .S2(\输出Q [2]), .S1(\输出Q [1]), .Cout(\进位_借位 ), .S0(\输出Q [0]), .Mode(\Mode_0正计数_1倒计数 ));

  // Other names for the same wires on the sheet: Cout = \进位_借位 ; Din[3:0] = \异步预置 ; En = \使能 ;
  //   Mode = \Mode_0正计数_1倒计数 ; PreSet = \异步置位控制 ; Q[3:0] = \输出Q 

  // Notes on the sheet:
  //   正计数到9，倒计数到0时输出为1
endmodule

// 状态转换
module \BCD双向计数器状态转换_自动生成  (
  input  S3,
  input  S2,
  input  S1,
  input  S0,
  input  Mode,
  output N3,
  output N2,
  output N1,
  output N0
);

  wire and_1_out, and_2_out, and_3_out, and_4_out, and_5_out, and_6_out, and_7_out, and_8_out, and_9_out,
       and_10_out, and_11_out, and_12_out, and_13_out, and_14_out, and_15_out, and_16_out, not_1_out,
       not_2_out, not_3_out, not_4_out, not_5_out, not_6_out, not_7_out, not_8_out, not_9_out, not_10_out,
       not_11_out, not_12_out, not_13_out, not_14_out, not_15_out, not_16_out, not_17_out, not_18_out,
       not_19_out, not_20_out, not_21_out;

  not not_1 (not_1_out, S3);
  not not_2 (not_2_out, S2);
  not not_3 (not_3_out, S1);
  not not_4 (not_4_out, S0);
  not not_5 (not_5_out, Mode);
  not not_6 (not_6_out, S0);
  not not_7 (not_7_out, Mode);
  not not_8 (not_8_out, S2);
  not not_9 (not_9_out, Mode);
  not not_10 (not_10_out, S1);
  not not_11 (not_11_out, Mode);
  not not_12 (not_12_out, S0);
  not not_13 (not_13_out, S0);
  not not_14 (not_14_out, S3);
  not not_15 (not_15_out, S1);
  not not_16 (not_16_out, Mode);
  not not_17 (not_17_out, S0);
  not not_18 (not_18_out, Mode);
  not not_19 (not_19_out, S1);
  not not_20 (not_20_out, S0);
  not not_21 (not_21_out, S0);
  not not_22 (N0, S0);
  and and_1 (and_1_out, not_1_out, not_2_out, not_3_out, not_4_out, Mode);
  and and_2 (and_2_out, S2, S1, S0, not_5_out);
  and and_3 (and_3_out, S3, not_6_out, not_7_out);
  and and_4 (and_4_out, S3, S0, Mode);
  and and_5 (and_5_out, S3, S1);
  and and_6 (and_6_out, S3, S2);
  and and_7 (and_7_out, not_8_out, S1, S0, not_9_out);
  and and_8 (and_8_out, S2, not_10_out, not_11_out);
  and and_9 (and_9_out, S2, S0, Mode);
  and and_10 (and_10_out, S2, S1, not_12_out);
  and and_11 (and_11_out, S3, not_13_out, Mode);
  and and_12 (and_12_out, not_14_out, not_15_out, S0, not_16_out);
  and and_13 (and_13_out, S1, not_17_out, not_18_out);
  and and_14 (and_14_out, S1, S0, Mode);
  and and_15 (and_15_out, S2, not_19_out, not_20_out, Mode);
  and and_16 (and_16_out, S3, not_21_out, Mode);
  or or_1 (N3, and_1_out, and_2_out, and_3_out, and_4_out, and_5_out, and_6_out);
  or or_2 (N2, and_7_out, and_8_out, and_9_out, and_10_out, and_11_out);
  or or_3 (N1, and_12_out, and_13_out, and_14_out, and_15_out, and_16_out);
endmodule

module \BCD双向计数器输出函数_自动生成  (
  input  S3,
  input  S2,
  input  S1,
  input  S0,
  input  Mode,
  output Cout
);

  wire and_1_out, and_2_out, not_1_out, not_2_out, not_3_out, not_4_out, not_5_out, not_6_out, not_7_out;

  not not_1 (not_1_out, S3);
  not not_2 (not_2_out, S2);
  not not_3 (not_3_out, S1);
  not not_4 (not_4_out, S0);
  not not_5 (not_5_out, S2);
  not not_6 (not_6_out, S1);
  not not_7 (not_7_out, Mode);
  and and_1 (and_1_out, not_1_out, not_2_out, not_3_out, not_4_out, Mode);
  and and_2 (and_2_out, S3, not_5_out, not_6_out, S0, not_7_out);
  or or_1 (Cout, and_1_out, and_2_out);
endmodule

// 倒计数
module \双位十进制双向计数器  (
  input  CLK,
  input  \使能 ,
  input  \异步置位控制 ,
  input  [7:0] \异步预置 ,
  input  \Mode_0正计数_1倒计数 ,
  output [7:0] Q,
  output \进位_借位 
);

  wire \bcd双向计数器_可异步置位_1_进位_借位 , \bcd双向计数器_可异步置位_2_进位_借位 , not_1_out;

  \BCD双向计数器_可异步置位  \bcd双向计数器_可异步置位_1  (
    .CLK(CLK), .\使能 (\使能 ), .\异步置位控制 (\异步置位控制 ), .\异步预置 (\异步预置 [3:0]), .\Mode_0正计数_1倒计数 (\Mode_0正计数_1倒计数 ),
    .\输出Q (Q[3:0]), .\进位_借位 (\bcd双向计数器_可异步置位_1_进位_借位 ));
  not not_1 (not_1_out, \bcd双向计数器_可异步置位_1_进位_借位 );
  \BCD双向计数器_可异步置位  \bcd双向计数器_可异步置位_2  (
    .CLK(not_1_out), .\使能 (\使能 ), .\异步置位控制 (\异步置位控制 ), .\异步预置 (\异步预置 [7:4]),
    .\Mode_0正计数_1倒计数 (\Mode_0正计数_1倒计数 ), .\输出Q (Q[7:4]), .\进位_借位 (\bcd双向计数器_可异步置位_2_进位_借位 ));
  and and_1 (\进位_借位 , \bcd双向计数器_可异步置位_2_进位_借位 , \bcd双向计数器_可异步置位_1_进位_借位 );
  // Probe on Q

  // Other names for the same wires on the sheet: Cout = \进位_借位 ; Din[7:0] = \异步预置 ; Din0[3:0] = \异步预置 [3:0];
  //   Din1[3:0] = \异步预置 [7:4]; En = \使能 ; Mode = \Mode_0正计数_1倒计数 ; PreSet = \异步置位控制 

  // Notes on the sheet:
  //   正计数到9，倒计数到0时输出为1
endmodule

// 状态机
module \红绿灯状态机_自动生成  (
  input  S2,
  input  S1,
  input  S0,
  input  T1,
  input  T2,
  input  T3,
  input  T4,
  input  EMERG,
  output N2,
  output N1,
  output N0
);

  wire and_1_out, and_2_out, and_3_out, and_4_out, and_5_out, and_6_out, and_7_out, and_8_out, and_9_out,
       and_10_out, and_11_out, and_12_out, and_13_out, not_1_out, not_2_out, not_3_out, not_4_out, not_5_out,
       not_6_out, not_7_out, not_8_out, not_9_out, not_10_out, not_11_out, not_12_out, not_13_out,
       not_14_out, not_15_out, not_16_out, not_17_out, not_18_out, not_19_out, not_20_out, not_21_out,
       not_22_out, not_23_out, not_24_out, not_25_out, not_26_out, not_27_out, not_28_out, not_29_out,
       not_30_out, not_31_out, not_32_out, not_33_out, not_34_out, not_35_out, not_36_out, not_37_out;

  not not_1 (not_1_out, S2);
  not not_2 (not_2_out, S1);
  not not_3 (not_3_out, S0);
  not not_4 (not_4_out, S2);
  not not_5 (not_5_out, S1);
  not not_6 (not_6_out, S2);
  not not_7 (not_7_out, S0);
  not not_8 (not_8_out, S2);
  not not_9 (not_9_out, S1);
  not not_10 (not_10_out, S0);
  not not_11 (not_11_out, S2);
  not not_12 (not_12_out, S1);
  not not_13 (not_13_out, EMERG);
  not not_14 (not_14_out, S2);
  not not_15 (not_15_out, S0);
  not not_16 (not_16_out, EMERG);
  not not_17 (not_17_out, S2);
  not not_18 (not_18_out, S0);
  not not_19 (not_19_out, T3);
  not not_20 (not_20_out, EMERG);
  not not_21 (not_21_out, S2);
  not not_22 (not_22_out, T4);
  not not_23 (not_23_out, EMERG);
  not not_24 (not_24_out, S2);
  not not_25 (not_25_out, S1);
  not not_26 (not_26_out, S0);
  not not_27 (not_27_out, EMERG);
  not not_28 (not_28_out, S2);
  not not_29 (not_29_out, S1);
  not not_30 (not_30_out, T2);
  not not_31 (not_31_out, EMERG);
  not not_32 (not_32_out, S2);
  not not_33 (not_33_out, S0);
  not not_34 (not_34_out, EMERG);
  not not_35 (not_35_out, S2);
  not not_36 (not_36_out, T4);
  not not_37 (not_37_out, EMERG);
  and and_1 (and_1_out, not_1_out, not_2_out, not_3_out, EMERG);
  and and_2 (and_2_out, not_4_out, not_5_out, S0, EMERG);
  and and_3 (and_3_out, not_6_out, S1, not_7_out, EMERG);
  and and_4 (and_4_out, not_8_out, S1, S0, EMERG);
  and and_5 (and_5_out, S2, not_9_out, not_10_out, EMERG);
  and and_6 (and_6_out, not_11_out, not_12_out, S0, T2, not_13_out);
  and and_7 (and_7_out, not_14_out, S1, not_15_out, T3, not_16_out);
  and and_8 (and_8_out, not_17_out, S1, not_18_out, not_19_out, not_20_out);
  and and_9 (and_9_out, not_21_out, S1, S0, not_22_out, not_23_out);
  and and_10 (and_10_out, not_24_out, not_25_out, not_26_out, T1, not_27_out);
  and and_11 (and_11_out, not_28_out, not_29_out, S0, not_30_out, not_31_out);
  and and_12 (and_12_out, not_32_out, S1, not_33_out, T3, not_34_out);
  and and_13 (and_13_out, not_35_out, S1, S0, not_36_out, not_37_out);
  or or_1 (N2, and_1_out, and_2_out, and_3_out, and_4_out, and_5_out);
  or or_2 (N1, and_6_out, and_7_out, and_8_out, and_9_out);
  or or_3 (N0, and_10_out, and_11_out, and_12_out, and_13_out);
endmodule

// 输出函数
module \红绿灯状态输出函数_真值表  (
  input  S2,
  input  S1,
  input  S0,
  output R1,
  output Y1,
  output G1,
  output R2,
  output Y2,
  output G2,
  output PASS1,
  output PASS2
);

  wire not_1_out, not_2_out, not_3_out, not_4_out, not_6_out, not_7_out, not_8_out;

  or or_1 (R1, S1, S2);
  not not_1 (not_1_out, S1);
  not not_2 (not_2_out, S2);
  not not_3 (not_3_out, S1);
  not not_4 (not_4_out, S0);
  not not_5 (R2, S1);
  and and_1 (Y2, S1, S0);
  not not_6 (not_6_out, S0);
  not not_7 (not_7_out, S2);
  not not_8 (not_8_out, S1);
  and and_2 (Y1, not_1_out, S0);
  and and_3 (G1, not_2_out, not_3_out, not_4_out);
  and and_4 (G2, S1, not_6_out);
  and and_5 (PASS1, not_7_out, not_8_out);

  assign PASS2 = S1;
endmodule
